# Fritzing sketch ARM_circuit_Diagram_1 (saved by Fritzing 0.9.3b)

parts:
  Part1 = Arduino Uno (Rev3)
  Bluetooth_Module = Bluetooth HC-05 Macho
  Base = Basic Servo
  Joint_1 = Basic Servo
  Joint_2 = Basic Servo
  M2 = DC Motor
  6v_power = Power plug
  12v_power = Power plug
  M3 = L293D Motor Driver
  S4 = SPST Switch [package=r_sw_th]

nets:
  N1: Part1.D9_PWM, Base.pulse
  N2: Part1.D10_PWM/SS, Joint_1.pulse
  N3: Part1.D11_PWM/MOSI, Joint_2.pulse
  GND: Part1.GND, Bluetooth_Module.GND, Base.gnd, Joint_1.gnd, Joint_2.gnd, 6v_power.GND, 12v_power.GND
  N4: Part1.D2, Bluetooth_Module.TXD
  N5: Part1.D3_PWM, Bluetooth_Module.RXD
  N6: Part1.D6_PWM, M3.pin_6
  N7: Part1.D7, M3.pin_5
  5V: Part1.5V, Bluetooth_Module.VCC
  VCC: Base.vcc, Joint_1.vcc, Joint_2.vcc, 6v_power.VCC
  N8: M2.pin_1, M3.pin_9
  N9: M2.pin_2, M3.pin_10
  N10: 12v_power.VCC, S4.O
